# Fritzing sketch Connections (saved by Fritzing 0.9.3b)
breadboards: 1

parts:
  Part2 = Arduino Uno (Rev3)
  U1 = LCD-16X2 [package=lcd-16x2]
  U2 = POT [package=pot_alpha_rv16af-20]
  HC-SR04_Sensor_1 = HC-SR04 Ultrasonic Distance Sensor
  Part3 = InvenSense MPU6050

nets:
  N1: Part2.A4/SDA, Part3.SDA
  N2: Part2.A5/SCL, Part3.SCL
  N3: Part2.D9_PWM, HC-SR04_Sensor_1.TRIG
  N4: Part2.D10_PWM/SS, HC-SR04_Sensor_1.ECHO
  N5: Part2.D11_PWM/MOSI, U1.E
  N6: Part2.D12/MISO, U1.RS
  GND: Part2.GND, U1.VSS, U1.R_W, U1.K, U2.A, HC-SR04_Sensor_1.GND, Part3.GND
  N7: Part2.D2, U1.DB7
  N8: Part2.D3_PWM, U1.DB6
  N9: Part2.D4, U1.DB5
  N10: Part2.D5_PWM, U1.DB4
  VCC: Part2.5V, U1.VDD, U1.A, U2.E, HC-SR04_Sensor_1.VCC, Part3.VCC
  N11: U1.VO, U2.S
